# Fritzing sketch currentBreadboardDiagram (saved by Fritzing 0.9.3b)
breadboards: 2

parts:
  Arduino_Pro_Mini = Arduino Mini (Rev5)
  Raspberry_Pi_3 = Raspberry Pi 3 [part_number=RPI-3-V1.2]
  part = DS18B20 1-Wire Temperature Sensor [part_number=DS18B20]

nets:
  VCC: Arduino_Pro_Mini.VCC, Raspberry_Pi_3.5V
  GND: Arduino_Pro_Mini.GND, Raspberry_Pi_3.GND, part.GND
  5V: Arduino_Pro_Mini.5V, part.VDD
  N1: Arduino_Pro_Mini.A0, part.DQ
  N2: Arduino_Pro_Mini.TX, Raspberry_Pi_3.GIPO15
  N3: Arduino_Pro_Mini.RX, Raspberry_Pi_3.GIPO14
